# Fritzing sketch voice_control_car (saved by Fritzing 0.9.3b)

parts:
  S1 = H-Bridge with L298N
  M1 = Getriebemotor
  M2 = Getriebemotor
  M3 = Getriebemotor
  M4 = Getriebemotor
  VCC1 = Battery
  Part1 = Breakout Board for Electret Microphone
  Part2 = Arduino Uno (Rev3) - ICSP

nets:
  12V: S1.12V, VCC1.+, Part2.VIN
  GND: S1.GND, VCC1.-, Part2.GND
  N1: S1.IN1, Part2.D7
  N2: S1.IN2, Part2.D6_PWM
  N3: S1.IN3, Part2.D5_PWM
  N4: S1.IN4, Part2.D4
  N5: S1.M1-01, M2.pin_2, M4.pin_1
  N6: S1.M1-02, S1.ENA-5V, M2.pin_1, M4.pin_2
  N7: S1.M2-01, M1.pin_1, M3.pin_2
  N8: S1.M2-02, M1.pin_2, M3.pin_1
  VCC: Part1.VCC, Part2.5V
  N9: Part1.GND, Part2.D3_PWM
  N10: Part1.AUD, Part2.D2

custom parts:
  H-Bridge with L298N: h-bridge
